// Logisim project adders.circ as structural Verilog: 1 circuit, main circuit main
module main (
  input  A,
  input  B,
  input  A_2,
  input  B_2,
  input  Cin,
  output S,
  output C,
  output S_2,
  output Cout
);

  wire AND_2_out, AND_3_out, XOR_2_out;

  xor XOR (S, A, B);
  and AND (C, A, B);
  xor XOR_2 (XOR_2_out, A_2, B_2);
  xor XOR_3 (S_2, XOR_2_out, Cin);
  and AND_2 (AND_2_out, Cin, XOR_2_out);
  and AND_3 (AND_3_out, B_2, A_2);
  or OR (Cout, AND_2_out, AND_3_out);
endmodule
