// Logisim project MUX.circ as structural Verilog: 1 circuit, main circuit main
module main (
  input  in_1,
  input  in_2,
  input  in_3,
  input  E1,
  input  E3,
  input  E2,
  input  E4,
  input  C1,
  input  C0,
  output out_10,
  output out_11
);

  wire and_1_out, and_2_out, and_3_out, and_4_out, and_5_out, and_6_out, and_7_out, and_8_out, not_1_out,
       not_2_out, not_3_out, or_1_out, or_2_out;

  not not_1 (not_1_out, in_2);
  not not_2 (not_2_out, C1);
  and and_1 (and_1_out, in_1, not_1_out);
  and and_2 (and_2_out, in_2, in_3);
  and and_3 (and_3_out, E1, not_2_out);
  and and_4 (and_4_out, E3, C1);
  and and_5 (and_5_out, E2, not_2_out);
  and and_6 (and_6_out, E4, C1);
  or or_1 (or_1_out, and_3_out, and_4_out);
  or or_2 (or_2_out, and_5_out, and_6_out);
  or or_3 (out_10, and_1_out, and_2_out);
  not not_3 (not_3_out, C0);
  and and_7 (and_7_out, or_1_out, not_3_out);
  and and_8 (and_8_out, or_2_out, C0);
  or or_4 (out_11, and_7_out, and_8_out);
endmodule
