// Logisim project deduct_circuits.circ as structural Verilog: 1 circuit, main circuit main
module main (
  input  A,
  input  B,
  input  in_3,
  input  in_4,
  input  in_5,
  input  in_6,
  input  in_7,
  input  in_8,
  input  in_9,
  input  in_10,
  input  in_11,
  output S__f_A__B,
  output U____A_and_C__or__nA_and_nB_and_nC,
  output V____A_and_B_and_C__or__A_and_nB_and_nC,
  output W___not_B
);

  wire AND_2_out, AND_3_out, AND_4_out, AND_5_out, AND_out, not_1_out, not_2_out, not_3_out, not_4_out,
       not_5_out;

  not not_1 (not_1_out, in_5);
  not not_2 (not_2_out, in_7);
  not not_3 (not_3_out, in_8);
  and AND (AND_out, A, B);
  and AND_2 (AND_2_out, in_3, in_5);
  not not_4 (not_4_out, in_4);
  not not_5 (not_5_out, in_3);
  not NOT_6 (S__f_A__B, AND_out);
  and AND_3 (AND_3_out, not_4_out, not_5_out, not_1_out);
  and AND_4 (AND_4_out, in_6, in_8, in_7);
  and AND_5 (AND_5_out, not_2_out, in_6, not_3_out);
  not not_7 (W___not_B, in_10);
  or OR (U____A_and_C__or__nA_and_nB_and_nC, AND_2_out, AND_3_out);
  or OR_2 (V____A_and_B_and_C__or__A_and_nB_and_nC, AND_4_out, AND_5_out);
endmodule
